# Fritzing sketch Untitled Sketch (saved by Fritzing 0.9.3b)
circuit board: 6.90929cm x 3.42344cm
breadboards: 1

parts:
  IC1 = IC, DIP package, 14 pins [chip_label=TL084]
  R1 = Resistor [tolerance=±5% resistance=2k package="2512 [SMD]"]
  R2 = Rotary Potentiometer (Small) [maximum_resistance=9kΩ package=THT]
  R3 = Rotary Potentiometer (Small) [maximum_resistance=9kΩ package=THT]
  R4 = Resistor [tolerance=±5% resistance=1k package="2512 [SMD]"]
  R5 = Resistor [tolerance=±5% resistance=1k package="2512 [SMD]"]
  R6 = Resistor [tolerance=±5% resistance=5k package="2512 [SMD]"]
  R7 = Resistor [tolerance=±5% resistance=10k package="2010 [SMD]"]
  R8 = Resistor [tolerance=±5% resistance=10k package="2512 [SMD]"]
  C1 = Capacitor Polarized [package=cpol-radial-100uf-25v]
  C2 = Capacitor Polarized [package=cpol-radial-100uf-25v]
  R9 = Resistor [tolerance=±5% resistance=100k package="2512 [SMD]"]
  R10 = Resistor [tolerance=±5% resistance=10 package="2512 [SMD]"]
  R11 = Resistor [tolerance=±5% resistance=90.9k package="2512 [SMD]"]
  C3 = Tantalum Capacitor [capacitance=22nF package="C 6032 [SMD, tantalum]"]

nets:
  N1: IC1.pin1, R2.wiper, R4.Pin_0
  N2: IC1.pin2, R1.Pin_0, R3.leg1
  N3: IC1.pin5, R5.Pin_1, R6.Pin_0
  N4: IC1.pin6, R4.Pin_1, R8.Pin_0
  N5: IC1.pin7, R8.Pin_1, C1.-
  N6: IC1.pin8, R11.Pin_1, C3.+
  N7: IC1.pin9, R10.Pin_1, R11.Pin_0
  N8: IC1.pin10, R2.leg2, R3.leg2, R7.Pin_1, R9.Pin_1, R10.Pin_0, C3.-
  N9: IC1.pin13, R1.Pin_1, R2.leg1
  N10: IC1.pin14, R3.wiper, R5.Pin_0
  N11: R6.Pin_1, R7.Pin_0
  N12: C1.+, C2.-
  N13: C2.+, R9.Pin_0

notes:
  [ecg signal]
